# Fritzing sketch Schematic overview 01 (saved by Fritzing 1.0.1rc)

parts:
  F1 = Fan - 4 wire [package=THT]
  A1 = mini boost module [part_number="Mini 360 buck converter"]
  V1 = DC Power [voltage=24]
  U1 = ESP32-38PinWide [part_number=ESP32-38PinWide]
  TM1637 = TM1637  # not connected
  part = Rotary Encoder Pushbutton [mn="EC12 Rotary" mpn=Encoder package=THT]
  S1 = SWITCH-MOMENTARY-2 [package=tactile_switch_smd]  # not connected
  S2 = SWITCH-MOMENTARY-2 [package=tactile-pth]  # not connected
  U2 = Optocoupler [package=THT]  # not connected
  R1 = Resistor [tolerance=±5% power=0.25W resistance=180 package=THT]
  R2 = Resistor [tolerance=±5% power=0.25W resistance=1k package=THT]
  R3 = Resistor [tolerance=±5% power=0.25W resistance=1k package=THT]

nets:
  N1: F1.GND, A1.Pin_1, V1.V-
  N2: F1.Power, A1.Pin_2, V1.V+
  N3: F1.PWM, R1.Pin_1
  N4: F1.Tach, U1.GPIO26, R2.Pin_1
  N5: A1.Pin_3, U1.GND, part.EncoderPinC, part.SwitchPin2
  N6: A1.Pin_4, U1.VIN
  N7: U1.3.3, R2.Pin_0
  N8: U1.GPIO33, R3.Pin_1
  N9: U1.GPIO25, R1.Pin_0
  N10: U1.GPIO14, part.EncoderPinB
  N11: U1.GPIO12, part.EncoderPinA
  N12: part.SwitchPin1, R3.Pin_0

custom parts:
  Fan - 4 wire: Fan, 4 wire with tach.
  mini boost module: mini boost module.
  ESP32-38PinWide: Generic 38-Pin ESP32 with wide format (only access to one side of pins on a breadboard) based on Stephen Lilley's HiLetgo ESP-WROOM-32 ESP32 ESP-32S Development Board.
  TM1637: A 4 7-seg display
  Rotary Encoder Pushbutton: Rotary Encoder with pushbutton from SRPassives part EC12E20-24P24C-SW.
